// Digital circuit example.dig as structural Verilog
module example (
  input  clock,
  input  [31:0] VT,
  input  V0,
  input  V1,
  input  V2,
  input  V3,
  input  V5,
  input  V6,
  input  V7,
  input  V8,
  input  V4,
  input  start,
  output [31:0] SP
);

  wire _0_p3, _0_p4, _0_p5, _0_p6, _0_p7, _1_p4, _1_p5, _1_p6, _1_p8, _1_p9, _2_p4, _2_p5, _2_p6, _2_p7,
       _2_p9, _2_p10, _2_p11, _3_p4, _3_p5, _3_p6, _3_p8, _3_p9, _4_p4, _4_p5, _4_p7, _5_p6, _5_p7, _5_p11,
       _6_p4, _6_p5, _6_p6, _6_p7, _6_p9, _7_p6, _7_p7, _7_p10, _8_p6, and_1_out;

  and and_1 (and_1_out, start, clock);
  // node_module #(.generic("edge_weights := [4,8]; neighbourhood_size := 2;")) _0: pin names not known; wires that end beside it: V0, and_1_out, _0_p3, _0_p4, _0_p5, _0_p6, _0_p7
  // node_module #(.generic("edge_weights := [4,8,11]; neighbourhood_size := 3;")) _1: pin names not known; wires that end beside it: V1, and_1_out, _0_p6, _1_p4, _1_p5, _1_p6, _0_p3, _1_p8, _1_p9
  // node_module #(.generic("edge_weights := [8,7,4,2]; neighbourhood_size := 4;")) _2: pin names not known; wires that end beside it: V2, and_1_out, _1_p8, _2_p4, _2_p5, _2_p6, _2_p7, _1_p4, _2_p9, _2_p10, _2_p11
  // node_module #(.generic("edge_weights := [7, 9, 14]; neighbourhood_size := 3;")) _3: pin names not known; wires that end beside it: V3, and_1_out, _2_p9, _3_p4, _3_p5, _3_p6, _2_p4, _3_p8, _3_p9
  // node_module #(.generic("edge_weights := [9,10]; neighbourhood_size := 2;")) _4: pin names not known; wires that end beside it: V4, and_1_out, _3_p8, _4_p4, _4_p5, _3_p4, _4_p7
  // node_module #(.generic("edge_weights := [4, 14, 10, 2]; neighbourhood_size := 4;")) _5: pin names not known; wires that end beside it: V5, and_1_out, _2_p10, _3_p9, _4_p7, _5_p6, _5_p7, _2_p5, _3_p5, _4_p4, _5_p11
  // node_module #(.generic("edge_weights := [ 6, 2, 1]; neighbourhood_size := 3;")) _6: pin names not known; wires that end beside it: V6, and_1_out, _5_p11, _6_p4, _6_p5, _6_p6, _6_p7, _5_p6, _6_p9
  // node_module #(.generic("edge_weights := [8,11, 7,1]; neighbourhood_size := 4;")) _7: pin names not known; wires that end beside it: V7, and_1_out, _0_p7, _1_p9, _6_p9, _7_p6, _7_p7, _0_p4, _1_p5, _7_p10, _6_p4
  // node_module #(.generic("edge_weights := [2, 6, 7]; neighbourhood_size := 3;")) _8: pin names not known; wires that end beside it: V8, and_1_out, _2_p11, _6_p7, _7_p10, _8_p6, _2_p6, _6_p5, _7_p6
  // extract_path #(.generic("number_of_inputs := 9;")) extract_path_1: pin names not known; wires that end beside it: VT, and_1_out, _0_p5, _1_p6, _2_p7, _3_p6, _4_p5, _5_p7, _6_p6, _7_p7, _8_p6, SP
endmodule
