// Digital circuit node_module.dig as structural Verilog
module node_module (
  input  start,
  input  clock,
  output [31:0] own
);

  wire [31:0] cheapselector_1_out, lookuptable_1_out;

  wires_in #(.generic("in_nodes := args.in_nodes;")) wires_in_1 ();
  LookUpTable #(.Bits(32)) lookuptable_1 (.in0(start), .in1(start), .out(lookuptable_1_out));
  cheapSelector cheapselector_1 (.a(lookuptable_1_out), .out(cheapselector_1_out));  // open: b
  decreasing_mem decreasing_mem_1 (.clock(clock), .A(cheapselector_1_out), .\output (own));
  wires_out #(.generic("out_nodes := args.out_nodes; weights := args.weights;")) wires_out_1 (.in(own));

  // Notes on the sheet:
  //   clock: Hz: 50000
  //   contents of lookuptable_1 (hex, n*v repeats v):
  //   7fffffff
endmodule

/* Code that sets the parameters or builds the circuit:
out_nodes:=6;
weights:=[1,2,4,8,16,32];
in_nodes:=8;
*/

/* Code that sets the parameters or builds the circuit:
x_output_start := 33;
y_output_start := 8;
y_output_add:= 1;

x_input_start := 4;
y_input_start := 6;
y_input_add:= 1;

y_input_offset:=0;

for (i:=0;i<args.out_nodes;i++){
    output:=addComponent("Out",x_output_start,y_output_start+i*y_output_add);
    output.Bits=32;
    output.Label="OUT"+i;
}

for (i:=0;i<args.in_nodes;i++){
    if(args.in_nodes%2=0)
    {
	if(i>=args.in_nodes/2){
	   y_input_offset = 1;
	}
    }
    output:=addComponent("In",x_input_start,y_input_start+i*y_input_add + y_input_offset);
    output.Bits=32;
    output.Label="IN"+i;
}

addWire(x_input_start+3,y_input_start + args.in_nodes/2,15,10);
*/
